# Fritzing sketch Huzzah32_Tone_Piezo_WithPOT (saved by Fritzing 0.9.4)
breadboards: 1

parts:
  Part1 = Adafruit HUZZAH32 ESP32 Feather [part_number="Adafruit #3405"]
  Piezo = Piezo Speaker

nets:
  N1: Part1.A0_DAC2, Piezo.pin2
  N2: Part1.GND, Piezo.pin1

notes:
  GPIO #26
